# Fritzing sketch ESP826sensor (saved by Fritzing 0.9.3b)
breadboards: 2

parts:
  WeMos_D1_Mini3 = WeMos D1 Mini  # not connected
  LED1 = LED - 3mm [color="Red (633nm)" package="3 mm [THT]"]  # not connected
  LED2 = LED - 3mm [color="Yellow (592nm)" package="3 mm [THT]"]
  R1 = Resistor [tolerance=±5% resistance=220 package="0603 [SMD]"]
  U1 = SIP - 4 pins [part_number=SHT20 chip_label=SHT20 package="SIP (Single Inline) [THT]"]
  R2 = Resistor [tolerance=±5% resistance=1k package="0603 [SMD]"]
  LED3 = LED - 3mm [color="Green (565nm)" package="3 mm [THT]"]
  R3 = Resistor [tolerance=±5% resistance=470 package="0603 [SMD]"]
  Squix1 = OLED 0.96" 128x64 I2C SSD1306 (GND/VCC)
  Part1 = BH1750

nets:
  N1: LED2.anode, R3.Pin_0
  N2: R1.Pin_0, LED3.anode
  VCC: R1.Pin_1, U1.VCC, R2.Pin_1, R3.Pin_1, Squix1.VCC, Part1.VCC
  N3: U1.SDA, Squix1.SCA, Part1.SDA
  N4: U1.SCL, Squix1.SCL, Part1.SCL
  GND: U1.GND, Squix1.GND, Part1.GND

custom parts:
  SIP - 4 pins: A SIP stand-in part for whatever you want. With 4 pins on a 300 mil single inline package (SIP) footprint.
  OLED 0.96" 128x64 I2C SSD1306 (GND/VCC): OLED 0.96" 128x64 I2C SSD1306 Pinout: GND/VCC/SCL/SDA
  BH1750: Light Sensor
